// Logisim project Proje.circ as structural Verilog: 8 circuits, main circuit main
module main (
);

  wire clock_1_out, saatdevresi_1_out_2, saatdevresi_1_out_3, saatdevresi_1_out_4, saatdevresi_1_out_5,
       saatdevresi_1_out_6, saatdevresi_1_out_7, saatdevresi_1_out_8, saatdevresi_1_out_9,
       saatdevresi_1_out_10, saatdevresi_1_out_11, saatdevresi_1_out_12, saatdevresi_1_out_13,
       saatdevresi_1_out_14, saatdevresi_1_out_15, saatdevresi_1_out_16, saatdevresi_1_out_17,
       saatdevresi_1_out_18, saatdevresi_1_out_19, saatdevresi_1_out_20, saatdevresi_1_out_21,
       saatdevresi_1_out_22, saatdevresi_1_out_23, saatdevresi_1_out_24, saatdevresi_1_out_25,
       saatdevresi_1_out_26, saatdevresi_1_out_27, saatdevresi_1_out_28, saatdevresi_1_out_29,
       saatdevresi_1_out_30, saatdevresi_1_out_31, saatdevresi_1_out_32, saatdevresi_1_out_33,
       saatdevresi_1_out_34, saatdevresi_1_out_35, saatdevresi_1_out_36, saatdevresi_1_out_37,
       saatdevresi_1_out_38, saatdevresi_1_out_39, saatdevresi_1_out_40, saatdevresi_1_out_41,
       saatdevresi_1_out_42, saatdevresi_1_out_43;

  _7_Segment_Display u_7_segment_display_1 (
    .g(saatdevresi_1_out_8), .f(saatdevresi_1_out_7), .a(saatdevresi_1_out_2), .b(saatdevresi_1_out_3),
    .e(saatdevresi_1_out_6), .d(saatdevresi_1_out_5), .c(saatdevresi_1_out_4));  // open: dp
  SaatDevresi saatdevresi_1 (
    .C(clock_1_out), .out_2(saatdevresi_1_out_2), .out_3(saatdevresi_1_out_3), .out_4(saatdevresi_1_out_4),
    .out_5(saatdevresi_1_out_5), .out_6(saatdevresi_1_out_6), .out_7(saatdevresi_1_out_7),
    .out_8(saatdevresi_1_out_8), .out_9(saatdevresi_1_out_9), .out_10(saatdevresi_1_out_10),
    .out_11(saatdevresi_1_out_11), .out_12(saatdevresi_1_out_12), .out_13(saatdevresi_1_out_13),
    .out_14(saatdevresi_1_out_14), .out_15(saatdevresi_1_out_15), .out_16(saatdevresi_1_out_16),
    .out_17(saatdevresi_1_out_17), .out_18(saatdevresi_1_out_18), .out_19(saatdevresi_1_out_19),
    .out_20(saatdevresi_1_out_20), .out_21(saatdevresi_1_out_21), .out_22(saatdevresi_1_out_22),
    .out_23(saatdevresi_1_out_23), .out_24(saatdevresi_1_out_24), .out_25(saatdevresi_1_out_25),
    .out_26(saatdevresi_1_out_26), .out_27(saatdevresi_1_out_27), .out_28(saatdevresi_1_out_28),
    .out_29(saatdevresi_1_out_29), .out_30(saatdevresi_1_out_30), .out_31(saatdevresi_1_out_31),
    .out_32(saatdevresi_1_out_32), .out_33(saatdevresi_1_out_33), .out_34(saatdevresi_1_out_34),
    .out_35(saatdevresi_1_out_35), .out_36(saatdevresi_1_out_36), .out_37(saatdevresi_1_out_37),
    .out_38(saatdevresi_1_out_38), .out_39(saatdevresi_1_out_39), .out_40(saatdevresi_1_out_40),
    .out_41(saatdevresi_1_out_41), .out_42(saatdevresi_1_out_42), .out_43(saatdevresi_1_out_43));
  _7_Segment_Display u_7_segment_display_2 (
    .g(saatdevresi_1_out_15), .f(saatdevresi_1_out_14), .a(saatdevresi_1_out_9), .b(saatdevresi_1_out_10),
    .e(saatdevresi_1_out_13), .d(saatdevresi_1_out_12), .c(saatdevresi_1_out_11));  // open: dp
  _7_Segment_Display u_7_segment_display_3 (
    .g(saatdevresi_1_out_22), .f(saatdevresi_1_out_21), .a(saatdevresi_1_out_16), .b(saatdevresi_1_out_17),
    .e(saatdevresi_1_out_20), .d(saatdevresi_1_out_19), .c(saatdevresi_1_out_18));  // open: dp
  Clock clock_1 (.out(clock_1_out));
  _7_Segment_Display u_7_segment_display_4 (
    .g(saatdevresi_1_out_29), .f(saatdevresi_1_out_28), .a(saatdevresi_1_out_23), .b(saatdevresi_1_out_24),
    .e(saatdevresi_1_out_27), .d(saatdevresi_1_out_26), .c(saatdevresi_1_out_25));  // open: dp
  _7_Segment_Display u_7_segment_display_5 (
    .g(saatdevresi_1_out_36), .f(saatdevresi_1_out_35), .a(saatdevresi_1_out_30), .b(saatdevresi_1_out_31),
    .e(saatdevresi_1_out_34), .d(saatdevresi_1_out_33), .c(saatdevresi_1_out_32));  // open: dp
  _7_Segment_Display u_7_segment_display_6 (
    .g(saatdevresi_1_out_43), .f(saatdevresi_1_out_42), .a(saatdevresi_1_out_37), .b(saatdevresi_1_out_38),
    .e(saatdevresi_1_out_41), .d(saatdevresi_1_out_40), .c(saatdevresi_1_out_39));  // open: dp

  // Notes on the sheet:
  //   :
  //   .
endmodule

module Binary_to_7_Segment_Decoder (
  input  D,
  input  C,
  input  B,
  input  A,
  output a_2,
  output b_2,
  output c_2,
  output d_2,
  output e,
  output f,
  output g
);

  wire and_1_out, and_2_out, and_3_out, and_4_out, and_5_out, and_6_out, and_7_out, and_8_out, and_9_out,
       and_10_out, and_11_out, and_12_out, and_13_out, and_14_out, and_15_out, and_16_out, not_1_out,
       not_2_out, not_3_out, not_4_out, not_5_out, not_6_out, not_7_out, not_8_out, not_9_out, not_10_out,
       not_11_out, not_12_out, not_13_out, not_14_out, not_15_out, not_16_out, not_17_out, not_18_out,
       not_19_out, not_20_out, not_21_out;

  not not_1 (not_1_out, C);
  and and_1 (and_1_out, not_1_out, not_2_out);
  not not_2 (not_2_out, A);
  and and_2 (and_2_out, C, A);
  not not_3 (not_3_out, C);
  not not_4 (not_4_out, B);
  and and_3 (and_3_out, not_4_out, not_5_out);
  not not_5 (not_5_out, A);
  and and_4 (and_4_out, B, A);
  not not_6 (not_6_out, B);
  or or_1 (c_2, not_6_out, A, C);
  not not_7 (not_7_out, C);
  and and_5 (and_5_out, not_7_out, not_8_out);
  not not_8 (not_8_out, A);
  not not_9 (not_9_out, C);
  and and_6 (and_6_out, not_9_out, B);
  and and_7 (and_7_out, B, not_10_out);
  not not_10 (not_10_out, A);
  not not_11 (not_11_out, B);
  and and_8 (and_8_out, C, not_11_out, A);
  not not_12 (not_12_out, C);
  and and_9 (and_9_out, not_12_out, not_13_out);
  not not_13 (not_13_out, A);
  and and_10 (and_10_out, B, not_14_out);
  not not_14 (not_14_out, A);
  not not_15 (not_15_out, B);
  and and_11 (and_11_out, not_15_out, not_16_out);
  not not_16 (not_16_out, A);
  and and_12 (and_12_out, C, not_17_out);
  not not_17 (not_17_out, B);
  and and_13 (and_13_out, C, not_18_out);
  not not_18 (not_18_out, A);
  not not_19 (not_19_out, C);
  and and_14 (and_14_out, not_19_out, B);
  and and_15 (and_15_out, C, not_20_out);
  not not_20 (not_20_out, B);
  and and_16 (and_16_out, C, not_21_out);
  not not_21 (not_21_out, A);
  or or_2 (a_2, and_1_out, B, and_2_out, D);
  or or_3 (b_2, not_3_out, and_3_out, and_4_out);
  or or_4 (d_2, and_5_out, and_6_out, and_7_out, and_8_out, D);
  or or_5 (e, and_9_out, and_10_out);
  or or_6 (f, and_11_out, and_12_out, and_13_out, D);
  or or_7 (g, and_14_out, and_15_out, and_16_out, D);
endmodule

module Mod10_Counter__saniye (
  input  in_1,
  output out_2,
  output out_3,
  output out_4,
  output out_5,
  output out_6
);

  wire and_1_out, and_2_out, and_3_out, and_4_out, and_5_out, and_6_out, and_7_out, d_ff_4_qn, not_1_out,
       not_2_out, not_3_out, not_4_out, not_5_out, not_6_out, not_7_out, or_1_out, or_2_out, or_3_out;

  not not_1 (not_1_out, out_5);
  and and_1 (and_1_out, out_2, not_1_out);
  and and_2 (and_2_out, out_5, out_3, out_4);
  or or_1 (or_1_out, and_1_out, and_2_out);
  not not_2 (not_2_out, out_5);
  not not_3 (not_3_out, out_4);
  not not_4 (not_4_out, out_3);
  not not_5 (not_5_out, out_5);
  not not_6 (not_6_out, out_4);
  not not_7 (not_7_out, out_2);
  and and_3 (and_3_out, out_3, not_2_out);
  and and_4 (and_4_out, out_3, not_3_out);
  and and_5 (and_5_out, not_4_out, out_4, out_5);
  and and_6 (and_6_out, out_4, not_5_out);
  and and_7 (and_7_out, out_5, not_6_out, not_7_out);
  or or_2 (or_2_out, and_6_out, and_7_out);
  or or_3 (or_3_out, and_3_out, and_4_out, and_5_out);
  D_Flip_Flop d_ff_1 (.clk(in_1), .D(or_1_out), .Q(out_2));  // open: Qn, preset, en, reset
  D_Flip_Flop d_ff_2 (.clk(in_1), .D(or_3_out), .Q(out_3));  // open: Qn, preset, en, reset
  D_Flip_Flop d_ff_3 (.clk(in_1), .D(or_2_out), .Q(out_4));  // open: Qn, preset, en, reset
  D_Flip_Flop d_ff_4 (.clk(in_1), .D(d_ff_4_qn), .Q(out_5), .Qn(d_ff_4_qn));  // open: preset, en, reset
  and and_8 (out_6, out_5, out_2);
endmodule

module Mod6_Counter (
  input  in_1,
  input  in_2,
  output out_3,
  output out_4,
  output out_5,
  output out_6
);

  wire and_1_out, and_2_out, and_3_out, and_4_out, and_5_out, and_6_out, not_1_out, not_2_out, not_3_out,
       not_4_out, not_5_out, not_6_out, or_1_out, or_2_out, xor_1_out;

  and and_1 (and_1_out, in_1, out_5, out_4);
  and and_2 (and_2_out, out_3, not_1_out);
  not not_1 (not_1_out, in_1);
  not not_2 (not_2_out, out_5);
  and and_3 (and_3_out, not_2_out, out_3);
  and and_4 (and_4_out, out_4, not_3_out);
  not not_3 (not_3_out, out_5);
  and and_5 (and_5_out, out_4, not_4_out);
  not not_4 (not_4_out, in_1);
  not not_5 (not_5_out, out_3);
  not not_6 (not_6_out, out_4);
  and and_6 (and_6_out, not_5_out, not_6_out, out_5, in_1);
  xor xor_1 (xor_1_out, out_5, in_1);
  and and_7 (out_6, out_3, out_5, in_1);
  or or_1 (or_1_out, and_1_out, and_2_out, and_3_out);
  or or_2 (or_2_out, and_4_out, and_5_out, and_6_out);
  D_Flip_Flop d_ff_1 (.clk(in_2), .D(or_1_out), .Q(out_3));  // open: Qn, preset, en, reset
  D_Flip_Flop d_ff_2 (.clk(in_2), .D(or_2_out), .Q(out_4));  // open: Qn, preset, en, reset
  D_Flip_Flop d_ff_3 (.clk(in_2), .D(xor_1_out), .Q(out_5));  // open: Qn, preset, en, reset
endmodule

module Mod10_Counter__dakika (
  input  in_1,
  input  in_2,
  output out_3,
  output out_4,
  output out_5,
  output out_6,
  output out_7
);

  wire and_1_out, and_2_out, and_3_out, and_4_out, and_5_out, and_6_out, and_7_out, and_8_out, and_9_out,
       and_10_out, not_1_out, not_2_out, not_3_out, not_4_out, not_5_out, not_6_out, not_7_out, not_8_out,
       not_9_out, not_10_out, not_11_out, or_1_out, or_2_out, or_3_out, xor_1_out;

  not not_1 (not_1_out, in_1);
  not not_2 (not_2_out, out_6);
  not not_3 (not_3_out, out_3);
  not not_4 (not_4_out, out_4);
  not not_5 (not_5_out, out_5);
  not not_6 (not_6_out, out_6);
  not not_7 (not_7_out, in_1);
  not not_8 (not_8_out, out_3);
  not not_9 (not_9_out, out_5);
  not not_10 (not_10_out, out_6);
  not not_11 (not_11_out, in_1);
  and and_1 (and_1_out, out_3, not_1_out);
  and and_2 (and_2_out, out_3, not_2_out);
  and and_3 (and_3_out, out_4, out_5, out_6, in_1);
  and and_4 (and_4_out, not_3_out, not_4_out, out_5, out_6, in_1);
  and and_5 (and_5_out, out_4, not_5_out);
  and and_6 (and_6_out, out_4, out_5, not_6_out);
  and and_7 (and_7_out, out_4, out_5, not_7_out);
  and and_8 (and_8_out, not_8_out, not_9_out, out_6, in_1);
  and and_9 (and_9_out, out_5, not_10_out);
  and and_10 (and_10_out, out_5, not_11_out);
  xor xor_1 (xor_1_out, out_6, in_1);
  and and_11 (out_7, out_3, out_6, in_1);
  or or_1 (or_1_out, and_1_out, and_2_out, and_3_out);
  or or_2 (or_2_out, and_8_out, and_9_out, and_10_out);
  or or_3 (or_3_out, and_4_out, and_5_out, and_6_out, and_7_out);
  D_Flip_Flop d_ff_1 (.clk(in_2), .D(or_1_out), .Q(out_3));  // open: Qn, preset, en, reset
  D_Flip_Flop d_ff_2 (.clk(in_2), .D(or_3_out), .Q(out_4));  // open: Qn, preset, en, reset
  D_Flip_Flop d_ff_3 (.clk(in_2), .D(or_2_out), .Q(out_5));  // open: Qn, preset, en, reset
  D_Flip_Flop d_ff_4 (.clk(in_2), .D(xor_1_out), .Q(out_6));  // open: Qn, preset, en, reset
endmodule

module mod24__Birler (
  input  x,
  input  onlar_2,
  input  C,
  output Da,
  output Db,
  output Dc,
  output Dd,
  output z
);

  wire and_1_out, and_2_out, and_3_out, and_4_out, and_5_out, and_6_out, and_7_out, and_8_out, and_9_out,
       and_10_out, and_11_out, and_12_out, and_13_out, and_14_out, not_1_out, not_2_out, not_3_out,
       not_4_out, not_5_out, not_6_out, not_7_out, not_8_out, not_9_out, not_10_out, not_11_out, not_12_out,
       not_13_out, not_14_out, or_1_out, or_2_out, or_3_out, or_4_out;

  not not_1 (not_1_out, Dd);
  not not_2 (not_2_out, x);
  not not_3 (not_3_out, Db);
  not not_4 (not_4_out, onlar_2);
  not not_5 (not_5_out, Dc);
  not not_6 (not_6_out, Dd);
  not not_7 (not_7_out, x);
  not not_8 (not_8_out, Da);
  not not_9 (not_9_out, Dc);
  not not_10 (not_10_out, Dd);
  not not_11 (not_11_out, x);
  not not_12 (not_12_out, Dd);
  not not_13 (not_13_out, x);
  not not_14 (not_14_out, Db);
  and and_1 (and_1_out, Db, Dc, Dd, x);
  and and_2 (and_2_out, Da, not_1_out);
  and and_3 (and_3_out, Da, not_2_out);
  and and_4 (and_4_out, not_3_out, Dc, Dd, x, not_4_out);
  and and_5 (and_5_out, Db, not_5_out);
  and and_6 (and_6_out, Db, not_6_out);
  and and_7 (and_7_out, Db, not_7_out);
  and and_8 (and_8_out, not_8_out, not_9_out, Dd, x);
  and and_9 (and_9_out, Dc, not_10_out);
  and and_10 (and_10_out, Dc, not_11_out);
  and and_11 (and_11_out, not_12_out, x);
  and and_12 (and_12_out, Dd, not_13_out);
  and and_13 (and_13_out, not_14_out, Dc, Dd, x, onlar_2);
  and and_14 (and_14_out, Da, Dd, x);
  or or_1 (or_1_out, and_1_out, and_2_out, and_3_out);
  or or_2 (or_2_out, and_4_out, and_5_out, and_6_out, and_7_out);
  or or_3 (or_3_out, and_8_out, and_9_out, and_10_out);
  or or_4 (or_4_out, and_11_out, and_12_out);
  or or_5 (z, and_13_out, and_14_out);
  D_Flip_Flop d_ff_1 (.clk(C), .D(or_1_out), .Q(Da));  // open: Qn, preset, en, reset
  D_Flip_Flop d_ff_2 (.clk(C), .D(or_2_out), .Q(Db));  // open: Qn, preset, en, reset
  D_Flip_Flop d_ff_3 (.clk(C), .D(or_3_out), .Q(Dc));  // open: Qn, preset, en, reset
  D_Flip_Flop d_ff_4 (.clk(C), .D(or_4_out), .Q(Dd));  // open: Qn, preset, en, reset
endmodule

module mod24__onlar (
  input  x,
  input  C,
  output Da,
  output Db,
  output z
);

  wire and_1_out, and_2_out, and_3_out, and_4_out, not_1_out, not_2_out, not_3_out, not_4_out, or_1_out,
       or_2_out;

  not not_1 (not_1_out, x);
  not not_2 (not_2_out, Da);
  not not_3 (not_3_out, Db);
  not not_4 (not_4_out, x);
  and and_1 (and_1_out, Db, x);
  and and_2 (and_2_out, Da, not_1_out);
  and and_3 (and_3_out, not_2_out, not_3_out, x);
  and and_4 (and_4_out, Db, not_4_out);
  or or_1 (or_1_out, and_1_out, and_2_out);
  or or_2 (or_2_out, and_3_out, and_4_out);
  D_Flip_Flop d_ff_1 (.clk(C), .D(or_1_out), .Q(Da));  // open: Qn, preset, en, reset
  D_Flip_Flop d_ff_2 (.clk(C), .D(or_2_out), .Q(Db));  // open: Qn, preset, en, reset

  assign z = Da;
endmodule

module SaatDevresi (
  input  C,
  output out_2,
  output out_3,
  output out_4,
  output out_5,
  output out_6,
  output out_7,
  output out_8,
  output out_9,
  output out_10,
  output out_11,
  output out_12,
  output out_13,
  output out_14,
  output out_15,
  output out_16,
  output out_17,
  output out_18,
  output out_19,
  output out_20,
  output out_21,
  output out_22,
  output out_23,
  output out_24,
  output out_25,
  output out_26,
  output out_27,
  output out_28,
  output out_29,
  output out_30,
  output out_31,
  output out_32,
  output out_33,
  output out_34,
  output out_35,
  output out_36,
  output out_37,
  output out_38,
  output out_39,
  output out_40,
  output out_41,
  output out_42,
  output out_43
);

  wire mod6_counter_1_out_3, mod6_counter_1_out_4, mod6_counter_1_out_5, mod6_counter_1_out_6,
       mod6_counter_2_out_3, mod6_counter_2_out_4, mod6_counter_2_out_5, mod6_counter_2_out_6,
       mod10_counter_dakika_1_out_3, mod10_counter_dakika_1_out_4, mod10_counter_dakika_1_out_5,
       mod10_counter_dakika_1_out_6, mod10_counter_dakika_1_out_7, mod10_counter_saniye_1_out_2,
       mod10_counter_saniye_1_out_3, mod10_counter_saniye_1_out_4, mod10_counter_saniye_1_out_5,
       mod10_counter_saniye_1_out_6, mod24_birler_1_da, mod24_birler_1_db, mod24_birler_1_dc,
       mod24_birler_1_dd, mod24_birler_1_z, mod24_onlar_1_da, mod24_onlar_1_db, mod24_onlar_1_z;

  mod24__onlar mod24_onlar_1 (
    .x(mod24_birler_1_z), .C(C), .Da(mod24_onlar_1_da), .Db(mod24_onlar_1_db), .z(mod24_onlar_1_z));
  mod24__Birler mod24_birler_1 (
    .x(mod6_counter_1_out_6), .onlar_2(mod24_onlar_1_z), .C(C), .Da(mod24_birler_1_da),
    .Db(mod24_birler_1_db), .Dc(mod24_birler_1_dc), .Dd(mod24_birler_1_dd), .z(mod24_birler_1_z));
  Mod6_Counter mod6_counter_1 (
    .in_1(mod10_counter_dakika_1_out_7), .in_2(C), .out_3(mod6_counter_1_out_3),
    .out_4(mod6_counter_1_out_4), .out_5(mod6_counter_1_out_5), .out_6(mod6_counter_1_out_6));
  Mod10_Counter__dakika mod10_counter_dakika_1 (
    .in_1(mod6_counter_2_out_6), .in_2(C), .out_3(mod10_counter_dakika_1_out_3),
    .out_4(mod10_counter_dakika_1_out_4), .out_5(mod10_counter_dakika_1_out_5),
    .out_6(mod10_counter_dakika_1_out_6), .out_7(mod10_counter_dakika_1_out_7));
  Mod6_Counter mod6_counter_2 (
    .in_1(mod10_counter_saniye_1_out_6), .in_2(C), .out_3(mod6_counter_2_out_3),
    .out_4(mod6_counter_2_out_4), .out_5(mod6_counter_2_out_5), .out_6(mod6_counter_2_out_6));
  Mod10_Counter__saniye mod10_counter_saniye_1 (
    .in_1(C), .out_2(mod10_counter_saniye_1_out_2), .out_3(mod10_counter_saniye_1_out_3),
    .out_4(mod10_counter_saniye_1_out_4), .out_5(mod10_counter_saniye_1_out_5),
    .out_6(mod10_counter_saniye_1_out_6));
  Binary_to_7_Segment_Decoder binary_to_7_segment_decoder_1 (
    .D(1'b0), .C(1'b0), .B(mod24_onlar_1_da), .A(mod24_onlar_1_db), .a_2(out_2), .b_2(out_3), .c_2(out_4),
    .d_2(out_5), .e(out_6), .f(out_7), .g(out_8));
  Binary_to_7_Segment_Decoder binary_to_7_segment_decoder_2 (
    .D(mod24_birler_1_da), .C(mod24_birler_1_db), .B(mod24_birler_1_dc), .A(mod24_birler_1_dd), .a_2(out_9),
    .b_2(out_10), .c_2(out_11), .d_2(out_12), .e(out_13), .f(out_14), .g(out_15));
  Binary_to_7_Segment_Decoder binary_to_7_segment_decoder_3 (
    .D(1'b0), .C(mod6_counter_1_out_3), .B(mod6_counter_1_out_4), .A(mod6_counter_1_out_5), .a_2(out_16),
    .b_2(out_17), .c_2(out_18), .d_2(out_19), .e(out_20), .f(out_21), .g(out_22));
  Binary_to_7_Segment_Decoder binary_to_7_segment_decoder_4 (
    .D(mod10_counter_dakika_1_out_3), .C(mod10_counter_dakika_1_out_4), .B(mod10_counter_dakika_1_out_5),
    .A(mod10_counter_dakika_1_out_6), .a_2(out_23), .b_2(out_24), .c_2(out_25), .d_2(out_26), .e(out_27),
    .f(out_28), .g(out_29));
  Binary_to_7_Segment_Decoder binary_to_7_segment_decoder_5 (
    .D(1'b0), .C(mod6_counter_2_out_3), .B(mod6_counter_2_out_4), .A(mod6_counter_2_out_5), .a_2(out_30),
    .b_2(out_31), .c_2(out_32), .d_2(out_33), .e(out_34), .f(out_35), .g(out_36));
  Binary_to_7_Segment_Decoder binary_to_7_segment_decoder_6 (
    .D(mod10_counter_saniye_1_out_2), .C(mod10_counter_saniye_1_out_3), .B(mod10_counter_saniye_1_out_4),
    .A(mod10_counter_saniye_1_out_5), .a_2(out_37), .b_2(out_38), .c_2(out_39), .d_2(out_40), .e(out_41),
    .f(out_42), .g(out_43));
endmodule
